# Fritzing sketch XMasLights (saved by Fritzing 0.9.3b)

parts:
  Part1 = Arduino Uno (Rev3)
  RGB_SMD_LED1 = SMD RGB LED (WS2812) [package=5050]
  JACK1 = 2.1mm Barrel Jack with Terminal Block
  C1 = Capacitor Polarized [package=cpol-radial-1000uf-25v]

nets:
  N1: Part1.D3_PWM, RGB_SMD_LED1.DIn
  5V: Part1.5V, RGB_SMD_LED1.VDD, JACK1.POS, C1.+
  GND: Part1.GND, RGB_SMD_LED1.VSS, JACK1.NEG, C1.-
